# Fritzing sketch ESP8266_12E-FTDI (saved by Fritzing 0.9.2b)
breadboards: 1

parts:
  U1 = ESP8266 WiFi Module [part_number=ESP8266]
  Деталь1 = FTDI Basic Programmer
  BAT1 = Battery Holders [package=lipo-1100mAh]
  R1 = Resistor [tolerance=±5% resistance=10k package=THT]
  R2 = Resistor [tolerance=±5% resistance=10k package=THT]
  S1 = Toggle Switch [package=THT]
  S2 = Pushbutton [package=THT]
  R3 = Resistor [tolerance=±5% resistance=10k package=THT]
  R4 = Resistor [tolerance=±5% resistance=10k package=THT]

nets:
  N1: U1.RXD, Деталь1.TXO
  N2: U1.VCC, BAT1.+, R2.Pin_0, S2.leg1, R3.Pin_1, R4.Pin_1
  N3: U1.GPIO_0, S1.COM
  N4: U1.CH_PD, R4.Pin_0
  GND: U1.GND, Деталь1.GND, BAT1.-, R1.Pin_0, S1.L1
  N5: U1.TXD, Деталь1.RXI
  N6: U1.REST, S2.leg0, R3.Pin_0
  N7: R2.Pin_1, S1.L2

notes:
  GPIO0 : pull low to program
  REST : pull low to reset
  Note : DO NOT power the esp8266 from the FTDI 3V3

custom parts:
  ESP8266 WiFi Module: Generic WiFi Module based on the ESP8266 with onboard PCB antenna and UART communications
