# Fritzing sketch ESP8266_12E_breakout (saved by Fritzing 0.9.2b)
circuit board: 8.46667cm x 5.64444cm
breadboards: 1

parts:
  esp8266 = ESP8266 WiFi Module [part_number=ESP8266]
  R1 = Resistor [tolerance=±5% resistance=10k package=THT]
  R2 = Resistor [tolerance=±5% resistance=10k package=THT]
  S2 = Pushbutton [package=THT]
  R3 = Resistor [tolerance=±5% resistance=10k package=THT]
  R4 = Resistor [tolerance=±5% resistance=10k package=THT]
  S3 = Pushbutton [package=THT]
  HT7333 = TRANSISTOR_NPN [package=sot89]
  JP1 = Header 4 [package=screwterminal-3.5mm-4_lock]
  JP2 = Header 12 [package=1x12_machine-pin-header_lock.004]

nets:
  N1: esp8266.RXD, JP1.3, JP2.8
  N2: esp8266.VCC, R2.Pin_0, R3.Pin_0, R4.Pin_1, HT7333.E, JP2.6
  N3: esp8266.GPIO_0, R2.Pin_1, S3.leg1
  N4: esp8266.GPIO_2, JP2.11
  N5: esp8266.CH_PD, R4.Pin_0
  N6: esp8266.GND, R1.Pin_0, S2.leg1, S3.leg0, HT7333.B, JP1.1, JP2.12
  N7: esp8266.TXD, JP1.2, JP2.7
  N8: esp8266.GPIO_15, R1.Pin_1
  N9: esp8266.GPIO_4, JP2.9
  N10: esp8266.GPIO_5, JP2.10
  N11: esp8266.ADC_0, JP2.1
  N12: esp8266.GPIO_16, JP2.2
  N13: esp8266.GPIO_14, JP2.3
  N14: esp8266.GPIO_12, JP2.4
  N15: esp8266.GPIO_13, JP2.5
  N16: esp8266.REST, S2.leg0, R3.Pin_1
  N17: HT7333.C, JP1.4

notes:
  GPIO0 : pull low to program
  RST : pull low to reset
  Note : DO NOT power the esp8266 from the FTDI 3V3
  EN : pull HIGH
  RST : pull HIGH
  GPIO0 : pull HIGH
  GPIO15 : pull LOW

custom parts:
  ESP8266 WiFi Module: Generic WiFi Module based on the ESP8266 with onboard PCB antenna and UART communications
